# Fritzing sketch Riego_v1 (saved by Fritzing 0.9.3b)
breadboards: 1

parts:
  R1 = Resistor [tolerance=±5% resistance=220 package=THT]
  R2 = Resistor [tolerance=±5% resistance=220 package=THT]
  LED4 = LED - 5mm [color="Red (633nm)" package="5 mm [THT]"]
  LED5 = LED - 5mm [color="Red (633nm)" package="5 mm [THT]"]
  U2 = 2-Channel 5v Relay Shield [package=relay-2ch5v10a]
  M1 = DOIT Esp32 DevKit v1 (30 pins long, 11 pins width) [part_number=ESP32S-PIN30]
  X1 = USB Connectors [package=usb-microb]

nets:
  N1: R1.Pin_0, U2.IN1, M1.D23
  N2: R1.Pin_1, LED5.anode
  N3: R2.Pin_0, U2.IN2, M1.D22
  N4: R2.Pin_1, LED4.anode
  GND: LED4.cathode, LED5.cathode, U2.GND, M1.GND, X1.VBUS
  VCC: U2.VCC, M1.3V3
  VIN: M1.VIN, X1.GND

custom parts:
  2-Channel 5v Relay Shield: 2 Channel 5v Relay Shield w. 2x SPD-06VDC-SD-C
  DOIT Esp32 DevKit v1 (30 pins long, 11 pins width): The DOIT Esp32 DevKit v1 is one of the development board created by DOIT to evaluate the ESP-WROOM-32 module. It is based on the ESP32 microcontroller that boasts Wifi, Bluetooth, Ethernet and Low Power support all in a single chip. (vanepp) made breadboard work, adjusted pin numbering and labels and reduced size of schematic and cleaned up pcb. This chip is 30pins long (2 x15) and 11 pins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
